# Fritzing sketch MiniGames (saved by Fritzing 1.0.5)
perfboards: 8

parts:
  S1 = Pushbutton [package="[THT]"]
  S2 = Pushbutton [package="[THT]"]
  S3 = Pushbutton [package="[THT]"]
  S4 = Pushbutton [package="[THT]"]
  buz1 = Piezo Buzzer  # not connected
  OLED_I2C1 = OLED 128x64 I2C Monochrome Display  # not connected
  Mod1 = TP4056 [part_number=TP4056]  # not connected
  A1 = Esp32-c3 super mini  # not connected
  S5 = Toggle Switch [package=THT]  # not connected
  Componente1 = LilyPad Coin Cell Battery Holder
  S6 = Toggle Switch [package=THT]
  A3 = ESP32-S3 zero

nets:
  N1: S1.Pin_1, S1.Pin_2
  N2: S1.Pin_3, S1.Pin_4
  N3: S2.Pin_1, S2.Pin_2
  N4: S2.Pin_3, S2.Pin_4
  N5: S3.Pin_1, S3.Pin_2
  N6: S3.Pin_3, S3.Pin_4
  N7: S4.Pin_1, S4.Pin_2
  N8: S4.Pin_3, S4.Pin_4
  N9: Componente1.+, S6.COM
  N10: S6.L2, A3.Pin_3

custom parts:
  Piezo Buzzer: Part from https://www.nutsvolts.com/magazine/article/november2012_SmileysWorkshop. Breadboard and icon images modified to be 0.3" in spacing and be more similar to the actual physical part.
  TP4056: TP4056 Lithium battery charger / protection module. (this one has the pins on .1 boundaried unlike the original)
  Esp32-c3 super mini: ESP32-C3 Development Board ESP32 SuperMini Development Board ESP32 Development Board WiFi Bluetooth.
  ESP32-S3 zero: ESP32-S3 Mini Development Board, Based on ESP32-S3FH4R2 Dual-Core Processor, 240MHz Running Frequency, 2.4GHz Wi-Fi & Bluetooth 5.
